// Logisim project AU194011FinalProject.circ as structural Verilog
module Binary_Cell (
  input  Select,
  input  Input,
  input  Read_Write,
  output Output
);

  wire and_1_out, and_2_out, nor_1_out, nor_2_out, not_1_out, not_2_out;

  not not_1 (not_1_out, Input);
  and and_1 (and_1_out, Select, not_1_out, not_2_out);
  and and_2 (and_2_out, Select, Input, not_2_out);
  not not_2 (not_2_out, Read_Write);
  nor nor_1 (nor_1_out, and_1_out, nor_2_out);
  nor nor_2 (nor_2_out, and_2_out, nor_1_out);
  and and_3 (Output, Select, nor_1_out, Read_Write);
endmodule

module _32_4_RAM_Memory (
  input  I2,
  input  I3,
  input  I4,
  input  I1,
  input  Read_Write,
  input  in_6,
  input  [4:0] in_7,
  output [3:0] out_8
);

  wire binary_cell_1_output, binary_cell_2_output, binary_cell_3_output, binary_cell_4_output,
       binary_cell_5_output, binary_cell_6_output, binary_cell_7_output, binary_cell_8_output,
       binary_cell_9_output, binary_cell_10_output, binary_cell_11_output, binary_cell_12_output,
       binary_cell_13_output, binary_cell_14_output, binary_cell_15_output, binary_cell_16_output,
       binary_cell_17_output, binary_cell_18_output, binary_cell_19_output, binary_cell_20_output,
       binary_cell_21_output, binary_cell_22_output, binary_cell_23_output, binary_cell_24_output,
       binary_cell_25_output, binary_cell_26_output, binary_cell_27_output, binary_cell_28_output,
       binary_cell_29_output, binary_cell_30_output, binary_cell_31_output, binary_cell_32_output,
       binary_cell_33_output, binary_cell_34_output, binary_cell_35_output, binary_cell_36_output,
       binary_cell_37_output, binary_cell_38_output, binary_cell_39_output, binary_cell_40_output,
       binary_cell_41_output, binary_cell_42_output, binary_cell_43_output, binary_cell_44_output,
       binary_cell_45_output, binary_cell_46_output, binary_cell_47_output, binary_cell_48_output,
       binary_cell_49_output, binary_cell_50_output, binary_cell_51_output, binary_cell_52_output,
       binary_cell_53_output, binary_cell_54_output, binary_cell_55_output, binary_cell_56_output,
       binary_cell_57_output, binary_cell_58_output, binary_cell_59_output, binary_cell_60_output,
       binary_cell_61_output, binary_cell_62_output, binary_cell_63_output, binary_cell_64_output,
       binary_cell_65_output, binary_cell_66_output, binary_cell_67_output, binary_cell_68_output,
       binary_cell_69_output, binary_cell_70_output, binary_cell_71_output, binary_cell_72_output,
       binary_cell_73_output, binary_cell_74_output, binary_cell_75_output, binary_cell_76_output,
       binary_cell_77_output, binary_cell_78_output, binary_cell_79_output, binary_cell_80_output,
       binary_cell_81_output, binary_cell_82_output, binary_cell_83_output, binary_cell_84_output,
       binary_cell_85_output, binary_cell_86_output, binary_cell_87_output, binary_cell_88_output,
       binary_cell_89_output, binary_cell_90_output, binary_cell_91_output, binary_cell_92_output,
       binary_cell_93_output, binary_cell_94_output, binary_cell_95_output, binary_cell_96_output,
       binary_cell_97_output, binary_cell_98_output, binary_cell_99_output, binary_cell_100_output,
       binary_cell_101_output, binary_cell_102_output, binary_cell_103_output, binary_cell_104_output,
       binary_cell_105_output, binary_cell_106_output, binary_cell_107_output, binary_cell_108_output,
       binary_cell_109_output, binary_cell_110_output, binary_cell_111_output, binary_cell_112_output,
       binary_cell_113_output, binary_cell_114_output, binary_cell_115_output, binary_cell_116_output,
       binary_cell_117_output, binary_cell_118_output, binary_cell_119_output, binary_cell_120_output,
       binary_cell_121_output, binary_cell_122_output, binary_cell_123_output, binary_cell_124_output,
       binary_cell_125_output, binary_cell_126_output, binary_cell_127_output, binary_cell_128_output,
       decoder_1_out0, decoder_1_out1, decoder_1_out2, decoder_1_out3, decoder_1_out4, decoder_1_out5,
       decoder_1_out6, decoder_1_out7, decoder_1_out8, decoder_1_out9, decoder_1_out10, decoder_1_out11,
       decoder_1_out12, decoder_1_out13, decoder_1_out14, decoder_1_out15, decoder_1_out16, decoder_1_out17,
       decoder_1_out18, decoder_1_out19, decoder_1_out20, decoder_1_out21, decoder_1_out22, decoder_1_out23,
       decoder_1_out24, decoder_1_out25, decoder_1_out26, decoder_1_out27, decoder_1_out28, decoder_1_out29,
       decoder_1_out30, decoder_1_out31;

  Decoder #(.select(5)) decoder_1 (
    .out0(decoder_1_out0), .out1(decoder_1_out1), .out2(decoder_1_out2), .out3(decoder_1_out3),
    .out4(decoder_1_out4), .out5(decoder_1_out5), .out6(decoder_1_out6), .out7(decoder_1_out7),
    .out8(decoder_1_out8), .out9(decoder_1_out9), .out10(decoder_1_out10), .out11(decoder_1_out11),
    .out12(decoder_1_out12), .out13(decoder_1_out13), .out14(decoder_1_out14), .out15(decoder_1_out15),
    .out16(decoder_1_out16), .out17(decoder_1_out17), .out18(decoder_1_out18), .out19(decoder_1_out19),
    .out20(decoder_1_out20), .out21(decoder_1_out21), .out22(decoder_1_out22), .out23(decoder_1_out23),
    .out24(decoder_1_out24), .out25(decoder_1_out25), .out26(decoder_1_out26), .out27(decoder_1_out27),
    .out28(decoder_1_out28), .out29(decoder_1_out29), .out30(decoder_1_out30), .out31(decoder_1_out31),
    .sel(in_7), .en(in_6));
  Binary_Cell binary_cell_1 (
    .Select(decoder_1_out0), .Input(I1), .Read_Write(Read_Write), .Output(binary_cell_1_output));
  Binary_Cell binary_cell_2 (
    .Select(decoder_1_out1), .Input(I1), .Read_Write(Read_Write), .Output(binary_cell_2_output));
  Binary_Cell binary_cell_3 (
    .Select(decoder_1_out2), .Input(I1), .Read_Write(Read_Write), .Output(binary_cell_3_output));
  Binary_Cell binary_cell_4 (
    .Select(decoder_1_out3), .Input(I1), .Read_Write(Read_Write), .Output(binary_cell_4_output));
  Binary_Cell binary_cell_5 (
    .Select(decoder_1_out4), .Input(I1), .Read_Write(Read_Write), .Output(binary_cell_5_output));
  Binary_Cell binary_cell_6 (
    .Select(decoder_1_out5), .Input(I1), .Read_Write(Read_Write), .Output(binary_cell_6_output));
  Binary_Cell binary_cell_7 (
    .Select(decoder_1_out6), .Input(I1), .Read_Write(Read_Write), .Output(binary_cell_7_output));
  Binary_Cell binary_cell_8 (
    .Select(decoder_1_out7), .Input(I1), .Read_Write(Read_Write), .Output(binary_cell_8_output));
  Binary_Cell binary_cell_9 (.Select(decoder_1_out8), .Input(I1), .Read_Write(I1), .Output(binary_cell_9_output));
  Binary_Cell binary_cell_10 (
    .Select(decoder_1_out9), .Input(I1), .Read_Write(Read_Write), .Output(binary_cell_10_output));
  Binary_Cell binary_cell_11 (
    .Select(decoder_1_out10), .Input(I1), .Read_Write(Read_Write), .Output(binary_cell_11_output));
  Binary_Cell binary_cell_12 (
    .Select(decoder_1_out11), .Input(I1), .Read_Write(Read_Write), .Output(binary_cell_12_output));
  Binary_Cell binary_cell_13 (
    .Select(decoder_1_out12), .Input(I1), .Read_Write(Read_Write), .Output(binary_cell_13_output));
  Binary_Cell binary_cell_14 (
    .Select(decoder_1_out13), .Input(I1), .Read_Write(Read_Write), .Output(binary_cell_14_output));
  Binary_Cell binary_cell_15 (
    .Select(decoder_1_out14), .Input(I1), .Read_Write(Read_Write), .Output(binary_cell_15_output));
  Binary_Cell binary_cell_16 (
    .Select(decoder_1_out15), .Input(I1), .Read_Write(Read_Write), .Output(binary_cell_16_output));
  Binary_Cell binary_cell_17 (
    .Select(decoder_1_out16), .Input(I1), .Read_Write(Read_Write), .Output(binary_cell_17_output));
  Binary_Cell binary_cell_18 (
    .Select(decoder_1_out17), .Input(I1), .Read_Write(Read_Write), .Output(binary_cell_18_output));
  Binary_Cell binary_cell_19 (
    .Select(decoder_1_out18), .Input(I1), .Read_Write(Read_Write), .Output(binary_cell_19_output));
  Binary_Cell binary_cell_20 (
    .Select(decoder_1_out19), .Input(I1), .Read_Write(Read_Write), .Output(binary_cell_20_output));
  Binary_Cell binary_cell_21 (
    .Select(decoder_1_out20), .Input(I1), .Read_Write(Read_Write), .Output(binary_cell_21_output));
  Binary_Cell binary_cell_22 (
    .Select(decoder_1_out21), .Input(I1), .Read_Write(Read_Write), .Output(binary_cell_22_output));
  Binary_Cell binary_cell_23 (
    .Select(decoder_1_out22), .Input(I1), .Read_Write(Read_Write), .Output(binary_cell_23_output));
  Binary_Cell binary_cell_24 (
    .Select(decoder_1_out23), .Input(I1), .Read_Write(Read_Write), .Output(binary_cell_24_output));
  Binary_Cell binary_cell_25 (
    .Select(decoder_1_out24), .Input(I1), .Read_Write(Read_Write), .Output(binary_cell_25_output));
  Binary_Cell binary_cell_26 (
    .Select(decoder_1_out25), .Input(I1), .Read_Write(Read_Write), .Output(binary_cell_26_output));
  Binary_Cell binary_cell_27 (
    .Select(decoder_1_out26), .Input(I1), .Read_Write(Read_Write), .Output(binary_cell_27_output));
  Binary_Cell binary_cell_28 (
    .Select(decoder_1_out27), .Input(I1), .Read_Write(Read_Write), .Output(binary_cell_28_output));
  Binary_Cell binary_cell_29 (
    .Select(decoder_1_out28), .Input(I1), .Read_Write(Read_Write), .Output(binary_cell_29_output));
  Binary_Cell binary_cell_30 (
    .Select(decoder_1_out29), .Input(I1), .Read_Write(Read_Write), .Output(binary_cell_30_output));
  Binary_Cell binary_cell_31 (
    .Select(decoder_1_out30), .Input(I1), .Read_Write(Read_Write), .Output(binary_cell_31_output));
  Binary_Cell binary_cell_32 (
    .Select(decoder_1_out31), .Input(I1), .Read_Write(Read_Write), .Output(binary_cell_32_output));
  or or_1 (out_8[0], binary_cell_32_output, binary_cell_31_output, binary_cell_30_output, binary_cell_29_output, binary_cell_28_output, binary_cell_27_output, binary_cell_26_output, binary_cell_25_output, binary_cell_24_output, binary_cell_23_output, binary_cell_22_output, binary_cell_21_output, binary_cell_20_output, binary_cell_19_output, binary_cell_18_output, binary_cell_17_output, binary_cell_16_output, binary_cell_15_output, binary_cell_14_output, binary_cell_13_output, binary_cell_12_output, binary_cell_11_output, binary_cell_10_output, binary_cell_9_output, binary_cell_8_output, binary_cell_7_output, binary_cell_6_output, binary_cell_5_output, binary_cell_4_output, binary_cell_3_output, binary_cell_2_output, binary_cell_1_output);
  Binary_Cell binary_cell_33 (
    .Select(decoder_1_out0), .Input(I2), .Read_Write(Read_Write), .Output(binary_cell_33_output));
  Binary_Cell binary_cell_34 (
    .Select(decoder_1_out1), .Input(I2), .Read_Write(Read_Write), .Output(binary_cell_34_output));
  Binary_Cell binary_cell_35 (
    .Select(decoder_1_out2), .Input(I2), .Read_Write(Read_Write), .Output(binary_cell_35_output));
  Binary_Cell binary_cell_36 (
    .Select(decoder_1_out3), .Input(I2), .Read_Write(Read_Write), .Output(binary_cell_36_output));
  Binary_Cell binary_cell_37 (
    .Select(decoder_1_out4), .Input(I2), .Read_Write(Read_Write), .Output(binary_cell_37_output));
  Binary_Cell binary_cell_38 (
    .Select(decoder_1_out5), .Input(I2), .Read_Write(Read_Write), .Output(binary_cell_38_output));
  Binary_Cell binary_cell_39 (
    .Select(decoder_1_out6), .Input(I2), .Read_Write(Read_Write), .Output(binary_cell_39_output));
  Binary_Cell binary_cell_40 (
    .Select(decoder_1_out7), .Input(I2), .Read_Write(Read_Write), .Output(binary_cell_40_output));
  Binary_Cell binary_cell_41 (.Select(decoder_1_out8), .Input(I2), .Read_Write(I1), .Output(binary_cell_41_output));
  Binary_Cell binary_cell_42 (
    .Select(decoder_1_out9), .Input(I2), .Read_Write(Read_Write), .Output(binary_cell_42_output));
  Binary_Cell binary_cell_43 (
    .Select(decoder_1_out10), .Input(I2), .Read_Write(Read_Write), .Output(binary_cell_43_output));
  Binary_Cell binary_cell_44 (
    .Select(decoder_1_out11), .Input(I2), .Read_Write(Read_Write), .Output(binary_cell_44_output));
  Binary_Cell binary_cell_45 (
    .Select(decoder_1_out12), .Input(I2), .Read_Write(Read_Write), .Output(binary_cell_45_output));
  Binary_Cell binary_cell_46 (
    .Select(decoder_1_out13), .Input(I2), .Read_Write(Read_Write), .Output(binary_cell_46_output));
  Binary_Cell binary_cell_47 (
    .Select(decoder_1_out14), .Input(I2), .Read_Write(Read_Write), .Output(binary_cell_47_output));
  Binary_Cell binary_cell_48 (
    .Select(decoder_1_out15), .Input(I2), .Read_Write(Read_Write), .Output(binary_cell_48_output));
  Binary_Cell binary_cell_49 (
    .Select(decoder_1_out16), .Input(I2), .Read_Write(Read_Write), .Output(binary_cell_49_output));
  Binary_Cell binary_cell_50 (
    .Select(decoder_1_out17), .Input(I2), .Read_Write(Read_Write), .Output(binary_cell_50_output));
  Binary_Cell binary_cell_51 (
    .Select(decoder_1_out18), .Input(I2), .Read_Write(Read_Write), .Output(binary_cell_51_output));
  Binary_Cell binary_cell_52 (
    .Select(decoder_1_out19), .Input(I2), .Read_Write(Read_Write), .Output(binary_cell_52_output));
  Binary_Cell binary_cell_53 (
    .Select(decoder_1_out20), .Input(I2), .Read_Write(Read_Write), .Output(binary_cell_53_output));
  Binary_Cell binary_cell_54 (
    .Select(decoder_1_out21), .Input(I2), .Read_Write(Read_Write), .Output(binary_cell_54_output));
  Binary_Cell binary_cell_55 (
    .Select(decoder_1_out22), .Input(I2), .Read_Write(Read_Write), .Output(binary_cell_55_output));
  Binary_Cell binary_cell_56 (
    .Select(decoder_1_out23), .Input(I2), .Read_Write(Read_Write), .Output(binary_cell_56_output));
  Binary_Cell binary_cell_57 (
    .Select(decoder_1_out24), .Input(I2), .Read_Write(Read_Write), .Output(binary_cell_57_output));
  Binary_Cell binary_cell_58 (
    .Select(decoder_1_out25), .Input(I2), .Read_Write(Read_Write), .Output(binary_cell_58_output));
  Binary_Cell binary_cell_59 (
    .Select(decoder_1_out26), .Input(I2), .Read_Write(Read_Write), .Output(binary_cell_59_output));
  Binary_Cell binary_cell_60 (
    .Select(decoder_1_out27), .Input(I2), .Read_Write(Read_Write), .Output(binary_cell_60_output));
  Binary_Cell binary_cell_61 (
    .Select(decoder_1_out28), .Input(I2), .Read_Write(Read_Write), .Output(binary_cell_61_output));
  Binary_Cell binary_cell_62 (
    .Select(decoder_1_out29), .Input(I2), .Read_Write(Read_Write), .Output(binary_cell_62_output));
  Binary_Cell binary_cell_63 (
    .Select(decoder_1_out30), .Input(I2), .Read_Write(Read_Write), .Output(binary_cell_63_output));
  Binary_Cell binary_cell_64 (
    .Select(decoder_1_out31), .Input(I2), .Read_Write(Read_Write), .Output(binary_cell_64_output));
  or or_2 (out_8[1], binary_cell_64_output, binary_cell_63_output, binary_cell_62_output, binary_cell_61_output, binary_cell_60_output, binary_cell_59_output, binary_cell_58_output, binary_cell_57_output, binary_cell_56_output, binary_cell_55_output, binary_cell_54_output, binary_cell_53_output, binary_cell_52_output, binary_cell_51_output, binary_cell_50_output, binary_cell_49_output, binary_cell_48_output, binary_cell_47_output, binary_cell_46_output, binary_cell_45_output, binary_cell_44_output, binary_cell_43_output, binary_cell_42_output, binary_cell_41_output, binary_cell_40_output, binary_cell_39_output, binary_cell_38_output, binary_cell_37_output, binary_cell_36_output, binary_cell_35_output, binary_cell_34_output, binary_cell_33_output);
  Binary_Cell binary_cell_65 (
    .Select(decoder_1_out0), .Input(I3), .Read_Write(Read_Write), .Output(binary_cell_65_output));
  Binary_Cell binary_cell_66 (
    .Select(decoder_1_out1), .Input(I3), .Read_Write(Read_Write), .Output(binary_cell_66_output));
  Binary_Cell binary_cell_67 (
    .Select(decoder_1_out2), .Input(I3), .Read_Write(Read_Write), .Output(binary_cell_67_output));
  Binary_Cell binary_cell_68 (
    .Select(decoder_1_out3), .Input(I3), .Read_Write(Read_Write), .Output(binary_cell_68_output));
  Binary_Cell binary_cell_69 (
    .Select(decoder_1_out4), .Input(I3), .Read_Write(Read_Write), .Output(binary_cell_69_output));
  Binary_Cell binary_cell_70 (
    .Select(decoder_1_out5), .Input(I3), .Read_Write(Read_Write), .Output(binary_cell_70_output));
  Binary_Cell binary_cell_71 (
    .Select(decoder_1_out6), .Input(I3), .Read_Write(Read_Write), .Output(binary_cell_71_output));
  Binary_Cell binary_cell_72 (
    .Select(decoder_1_out7), .Input(I3), .Read_Write(Read_Write), .Output(binary_cell_72_output));
  Binary_Cell binary_cell_73 (.Select(decoder_1_out8), .Input(I3), .Read_Write(I1), .Output(binary_cell_73_output));
  Binary_Cell binary_cell_74 (
    .Select(decoder_1_out9), .Input(I3), .Read_Write(Read_Write), .Output(binary_cell_74_output));
  Binary_Cell binary_cell_75 (
    .Select(decoder_1_out10), .Input(I3), .Read_Write(Read_Write), .Output(binary_cell_75_output));
  Binary_Cell binary_cell_76 (
    .Select(decoder_1_out11), .Input(I3), .Read_Write(Read_Write), .Output(binary_cell_76_output));
  Binary_Cell binary_cell_77 (
    .Select(decoder_1_out12), .Input(I3), .Read_Write(Read_Write), .Output(binary_cell_77_output));
  Binary_Cell binary_cell_78 (
    .Select(decoder_1_out13), .Input(I3), .Read_Write(Read_Write), .Output(binary_cell_78_output));
  Binary_Cell binary_cell_79 (
    .Select(decoder_1_out14), .Input(I3), .Read_Write(Read_Write), .Output(binary_cell_79_output));
  Binary_Cell binary_cell_80 (
    .Select(decoder_1_out15), .Input(I3), .Read_Write(Read_Write), .Output(binary_cell_80_output));
  Binary_Cell binary_cell_81 (
    .Select(decoder_1_out16), .Input(I3), .Read_Write(Read_Write), .Output(binary_cell_81_output));
  Binary_Cell binary_cell_82 (
    .Select(decoder_1_out17), .Input(I3), .Read_Write(Read_Write), .Output(binary_cell_82_output));
  Binary_Cell binary_cell_83 (
    .Select(decoder_1_out18), .Input(I3), .Read_Write(Read_Write), .Output(binary_cell_83_output));
  Binary_Cell binary_cell_84 (
    .Select(decoder_1_out19), .Input(I3), .Read_Write(Read_Write), .Output(binary_cell_84_output));
  Binary_Cell binary_cell_85 (
    .Select(decoder_1_out20), .Input(I3), .Read_Write(Read_Write), .Output(binary_cell_85_output));
  Binary_Cell binary_cell_86 (
    .Select(decoder_1_out21), .Input(I3), .Read_Write(Read_Write), .Output(binary_cell_86_output));
  Binary_Cell binary_cell_87 (
    .Select(decoder_1_out22), .Input(I3), .Read_Write(Read_Write), .Output(binary_cell_87_output));
  Binary_Cell binary_cell_88 (
    .Select(decoder_1_out23), .Input(I3), .Read_Write(Read_Write), .Output(binary_cell_88_output));
  Binary_Cell binary_cell_89 (
    .Select(decoder_1_out24), .Input(I3), .Read_Write(Read_Write), .Output(binary_cell_89_output));
  Binary_Cell binary_cell_90 (
    .Select(decoder_1_out25), .Input(I3), .Read_Write(Read_Write), .Output(binary_cell_90_output));
  Binary_Cell binary_cell_91 (
    .Select(decoder_1_out26), .Input(I3), .Read_Write(Read_Write), .Output(binary_cell_91_output));
  Binary_Cell binary_cell_92 (
    .Select(decoder_1_out27), .Input(I3), .Read_Write(Read_Write), .Output(binary_cell_92_output));
  Binary_Cell binary_cell_93 (
    .Select(decoder_1_out28), .Input(I3), .Read_Write(Read_Write), .Output(binary_cell_93_output));
  Binary_Cell binary_cell_94 (
    .Select(decoder_1_out29), .Input(I3), .Read_Write(Read_Write), .Output(binary_cell_94_output));
  Binary_Cell binary_cell_95 (
    .Select(decoder_1_out30), .Input(I3), .Read_Write(Read_Write), .Output(binary_cell_95_output));
  Binary_Cell binary_cell_96 (
    .Select(decoder_1_out31), .Input(I3), .Read_Write(Read_Write), .Output(binary_cell_96_output));
  or or_3 (out_8[2], binary_cell_96_output, binary_cell_95_output, binary_cell_94_output, binary_cell_93_output, binary_cell_92_output, binary_cell_91_output, binary_cell_90_output, binary_cell_89_output, binary_cell_88_output, binary_cell_87_output, binary_cell_86_output, binary_cell_85_output, binary_cell_84_output, binary_cell_83_output, binary_cell_82_output, binary_cell_81_output, binary_cell_80_output, binary_cell_79_output, binary_cell_78_output, binary_cell_77_output, binary_cell_76_output, binary_cell_75_output, binary_cell_74_output, binary_cell_73_output, binary_cell_72_output, binary_cell_71_output, binary_cell_70_output, binary_cell_69_output, binary_cell_68_output, binary_cell_67_output, binary_cell_66_output, binary_cell_65_output);
  Binary_Cell binary_cell_97 (
    .Select(decoder_1_out0), .Input(I4), .Read_Write(Read_Write), .Output(binary_cell_97_output));
  Binary_Cell binary_cell_98 (
    .Select(decoder_1_out1), .Input(I4), .Read_Write(Read_Write), .Output(binary_cell_98_output));
  Binary_Cell binary_cell_99 (
    .Select(decoder_1_out2), .Input(I4), .Read_Write(Read_Write), .Output(binary_cell_99_output));
  Binary_Cell binary_cell_100 (
    .Select(decoder_1_out3), .Input(I4), .Read_Write(Read_Write), .Output(binary_cell_100_output));
  Binary_Cell binary_cell_101 (
    .Select(decoder_1_out4), .Input(I4), .Read_Write(Read_Write), .Output(binary_cell_101_output));
  Binary_Cell binary_cell_102 (
    .Select(decoder_1_out5), .Input(I4), .Read_Write(Read_Write), .Output(binary_cell_102_output));
  Binary_Cell binary_cell_103 (
    .Select(decoder_1_out6), .Input(I4), .Read_Write(Read_Write), .Output(binary_cell_103_output));
  Binary_Cell binary_cell_104 (
    .Select(decoder_1_out7), .Input(I4), .Read_Write(Read_Write), .Output(binary_cell_104_output));
  Binary_Cell binary_cell_105 (.Select(decoder_1_out8), .Input(I4), .Read_Write(I1), .Output(binary_cell_105_output));
  Binary_Cell binary_cell_106 (
    .Select(decoder_1_out9), .Input(I4), .Read_Write(Read_Write), .Output(binary_cell_106_output));
  Binary_Cell binary_cell_107 (
    .Select(decoder_1_out10), .Input(I4), .Read_Write(Read_Write), .Output(binary_cell_107_output));
  Binary_Cell binary_cell_108 (
    .Select(decoder_1_out11), .Input(I4), .Read_Write(Read_Write), .Output(binary_cell_108_output));
  Binary_Cell binary_cell_109 (
    .Select(decoder_1_out12), .Input(I4), .Read_Write(Read_Write), .Output(binary_cell_109_output));
  Binary_Cell binary_cell_110 (
    .Select(decoder_1_out13), .Input(I4), .Read_Write(Read_Write), .Output(binary_cell_110_output));
  Binary_Cell binary_cell_111 (
    .Select(decoder_1_out14), .Input(I4), .Read_Write(Read_Write), .Output(binary_cell_111_output));
  Binary_Cell binary_cell_112 (
    .Select(decoder_1_out15), .Input(I4), .Read_Write(Read_Write), .Output(binary_cell_112_output));
  Binary_Cell binary_cell_113 (
    .Select(decoder_1_out16), .Input(I4), .Read_Write(Read_Write), .Output(binary_cell_113_output));
  Binary_Cell binary_cell_114 (
    .Select(decoder_1_out17), .Input(I4), .Read_Write(Read_Write), .Output(binary_cell_114_output));
  Binary_Cell binary_cell_115 (
    .Select(decoder_1_out18), .Input(I4), .Read_Write(Read_Write), .Output(binary_cell_115_output));
  Binary_Cell binary_cell_116 (
    .Select(decoder_1_out19), .Input(I4), .Read_Write(Read_Write), .Output(binary_cell_116_output));
  Binary_Cell binary_cell_117 (
    .Select(decoder_1_out20), .Input(I4), .Read_Write(Read_Write), .Output(binary_cell_117_output));
  Binary_Cell binary_cell_118 (
    .Select(decoder_1_out21), .Input(I4), .Read_Write(Read_Write), .Output(binary_cell_118_output));
  Binary_Cell binary_cell_119 (
    .Select(decoder_1_out22), .Input(I4), .Read_Write(Read_Write), .Output(binary_cell_119_output));
  Binary_Cell binary_cell_120 (
    .Select(decoder_1_out23), .Input(I4), .Read_Write(Read_Write), .Output(binary_cell_120_output));
  Binary_Cell binary_cell_121 (
    .Select(decoder_1_out24), .Input(I4), .Read_Write(Read_Write), .Output(binary_cell_121_output));
  Binary_Cell binary_cell_122 (
    .Select(decoder_1_out25), .Input(I4), .Read_Write(Read_Write), .Output(binary_cell_122_output));
  Binary_Cell binary_cell_123 (
    .Select(decoder_1_out26), .Input(I4), .Read_Write(Read_Write), .Output(binary_cell_123_output));
  Binary_Cell binary_cell_124 (
    .Select(decoder_1_out27), .Input(I4), .Read_Write(Read_Write), .Output(binary_cell_124_output));
  Binary_Cell binary_cell_125 (
    .Select(decoder_1_out28), .Input(I4), .Read_Write(Read_Write), .Output(binary_cell_125_output));
  Binary_Cell binary_cell_126 (
    .Select(decoder_1_out29), .Input(I4), .Read_Write(Read_Write), .Output(binary_cell_126_output));
  Binary_Cell binary_cell_127 (
    .Select(decoder_1_out30), .Input(I4), .Read_Write(Read_Write), .Output(binary_cell_127_output));
  Binary_Cell binary_cell_128 (
    .Select(decoder_1_out31), .Input(I4), .Read_Write(Read_Write), .Output(binary_cell_128_output));
  or or_4 (out_8[3], binary_cell_128_output, binary_cell_127_output, binary_cell_126_output, binary_cell_125_output, binary_cell_124_output, binary_cell_123_output, binary_cell_122_output, binary_cell_121_output, binary_cell_120_output, binary_cell_119_output, binary_cell_118_output, binary_cell_117_output, binary_cell_116_output, binary_cell_115_output, binary_cell_114_output, binary_cell_113_output, binary_cell_112_output, binary_cell_111_output, binary_cell_110_output, binary_cell_109_output, binary_cell_108_output, binary_cell_107_output, binary_cell_106_output, binary_cell_105_output, binary_cell_104_output, binary_cell_103_output, binary_cell_102_output, binary_cell_101_output, binary_cell_100_output, binary_cell_99_output, binary_cell_98_output, binary_cell_97_output);
endmodule
